// Logisim project project.circ as structural Verilog
module main (
  input  [31:0] in_1,
  output [7:0] out_2
);

  wire button_1_out, clock_1_out;

  Clock clock_1 (.out(clock_1_out));
  Button button_1 (.out(button_1_out));
  ROM #(.dataWidth(32)) rom_1 (.addr(out_2), .data(in_1));
  PC pc_1 (.clk(clock_1_out), .reset(button_1_out), .out_3(out_2));
endmodule

module PC (
  input  clk,
  input  reset,
  output [7:0] out_3
);

  wire [31:0] adder_1_out, register_1_q;

  Adder #(.width(32)) adder_1 (
    .a(32'h4), .b({register_1_q[31:10], out_3, register_1_q[1:0]}), .out(adder_1_out));  // open: cin, cout
  Register #(.width(32)) register_1 (
    .D(adder_1_out), .clk(clk), .Q({register_1_q[31:10], out_3, register_1_q[1:0]}), .clr(reset));  // open: en
endmodule
